# Fritzing sketch Project 2 (saved by Fritzing 0.9.4)
breadboards: 1

parts:
  Part1 = Arduino Uno (Rev3)
  R1 = Resistor [tolerance=±5% resistance=47k package=THT]
  SP1 = SPEAKER [package=pcb_mount_speaker]
  R2 = Resistor [tolerance=±5% resistance=47k package=THT]
  R3 = Resistor [tolerance=±5% resistance=47k package=THT]
  R4 = Resistor [tolerance=±5% resistance=47k package=THT]
  R5 = Resistor [tolerance=±5% resistance=47k package=THT]
  R6 = Resistor [tolerance=±5% resistance=47k package=THT]
  R7 = Resistor [tolerance=±5% resistance=47k package=THT]

nets:
  N1: Part1.D8, R4.Pin_1
  N2: Part1.D9_PWM, R7.Pin_1
  N3: Part1.D11_PWM/MOSI, SP1.+
  N4: Part1.D2, R1.Pin_0, R2.Pin_0, R3.Pin_0, R4.Pin_0, R5.Pin_0, R6.Pin_0, R7.Pin_0
  N5: Part1.D3_PWM, R1.Pin_1
  N6: Part1.D4, R2.Pin_1
  N7: Part1.D5_PWM, R3.Pin_1
  N8: Part1.D6_PWM, R6.Pin_1
  N9: Part1.D7, R5.Pin_1
  N10: Part1.GND, SP1.-

notes:
  Out to JFK Silver Dollar
  Out to JFK Half Dollar
  Out to SBA Silver Dollar
  Out to Silver Quarter, 1961
  Out to Silver Nickel, 1943
  Out to Penny from 1909
  Out to Silver Dime, 1964
